# Fritzing sketch Sembrani (saved by Fritzing 0.9.3b)
breadboards: 1

parts:
  Development_Board = DOIT Esp32 DevKit v1 (30 pins long, 11 pins width) [part_number=ESP32S-PIN30]
  Buzzer = Piezo Speaker
  Opto_O_Alerm = Sharp PC817 [package=THT]
  R1 = Resistor [tolerance=±5% resistance=220 package=THT]
  BAT1 = 12 battery [package=battery]
  RF_Receiver = SC2272 [chip_label=SC2272 package="SIP (Single Inline) [THT]"]
  U2 = Mini-360 DC-DC Buck converter [package=THT]
  Opto_O_Lock = Sharp PC817 [package=THT]
  Opto_O_Starter = Sharp PC817 [package=THT]
  Opto_I_RPM = Sharp PC817 [package=THT]
  Opto_Input_Lock = Sharp PC817 [package=THT]
  Contact_Key = Toggle Switch [package=THT]
  R5 = Resistor [tolerance=±5% resistance=1k package=THT]
  SP1 = SPEAKER [package=pcb_mount_speaker]
  R4 = Resistor [tolerance=±5% resistance=1k package=THT]
  R2 = Resistor [tolerance=±5% resistance=220 package=THT]
  R3 = Resistor [tolerance=±5% resistance=220 package=THT]
  Part1 = LCD1602-I2C

nets:
  GND: Development_Board.GND, Buzzer.pin1, Opto_O_Alerm.Pin_2, RF_Receiver.GND, U2.OUT-, Opto_O_Lock.Pin_2, Opto_O_Starter.Pin_2, Part1.GND
  N1: Development_Board.D21, Part1.SDA
  N2: Development_Board.D22, Part1.SCL
  N3: Development_Board.D25, RF_Receiver.D3
  N4: Development_Board.D26, RF_Receiver.D2
  N5: Development_Board.D27, RF_Receiver.D1
  N6: Development_Board.D14, RF_Receiver.D0
  N7: Development_Board.D12, RF_Receiver.VT
  N8: Development_Board.D13, Buzzer.pin2
  VIN: Development_Board.VIN, RF_Receiver.5v, U2.OUT+, Part1.VCC
  N9: Opto_O_Alerm.Pin_1, R1.Pin_0
  N10: Opto_O_Alerm.Pin_4, SP1.-
  N11: Opto_O_Alerm.Pin_3, BAT1.+, U2.IN+, Contact_Key.COM
  N12: BAT1.-, U2.IN-, Opto_I_RPM.Pin_2, Opto_Input_Lock.Pin_2, SP1.+
  N13: Opto_O_Lock.Pin_1, R2.Pin_0
  N14: Opto_O_Starter.Pin_1, R3.Pin_0
  N15: Opto_I_RPM.Pin_1, R4.Pin_1
  N16: Opto_Input_Lock.Pin_1, R5.Pin_1
  N17: Contact_Key.L1, R5.Pin_0

notes:
  12v
  5v

custom parts:
  DOIT Esp32 DevKit v1 (30 pins long, 11 pins width): The DOIT Esp32 DevKit v1 is one of the development board created by DOIT to evaluate the ESP-WROOM-32 module. It is based on the ESP32 microcontroller that boasts Wifi, Bluetooth, Ethernet and Low Power support all in a single chip. (vanepp) made breadboard work, adjusted pin numbering and labels and reduced size of schematic and cleaned up pcb. This chip is 30pins long (2 x15) and 11 pins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
  12 battery: 12V lead acid type battery, like the Husqvarna YTH2448 12V 35AH battery. This is the mini version 1/4 the size of the actual battery to be closer to typical breadboard parts (around 2in wide rathher than 7in). The pads in pcb are sized to accomidate up to 14ga wire (as these batterys will deliver high currents.)
  SC2272: Simple Part SC2272
  Mini-360 DC-DC Buck converter: Mini-360 DC-DC Buck converter. Tiny buck step down voltage converter, input voltage 4.75 to 23V output 1 to 17V adjustable. Available from ebay and the like.
  LCD1602-I2C: A standard character display, usually with 2x16 characters. Comes in many colors with LCM1602 IIC attached.
